# Fritzing sketch relogio nano (saved by Fritzing 0.9.2b)
breadboards: 1

parts:
  Componente1 = Arduino Nano (Rev3.0) (ICSP)
  U1 = 74HC595 [package="DIP16 [THT]"]
  R1 = Resistor [tolerance=±5% resistance=330 package=THT]
  R2 = Resistor [tolerance=±5% resistance=330 package=THT]
  R3 = Resistor [tolerance=±5% resistance=330 package=THT]
  R4 = Resistor [tolerance=±5% resistance=330 package=THT]
  R5 = Resistor [tolerance=±5% resistance=330 package=THT]
  R6 = Resistor [tolerance=±5% resistance=330 package=THT]
  R7 = Resistor [tolerance=±5% resistance=330 package=THT]
  R8 = Resistor [tolerance=±5% resistance=330 package=THT]
  U2 = 74HC595 [package="DIP16 [THT]"]
  R9 = Resistor [tolerance=±5% resistance=330 package=THT]
  R10 = Resistor [tolerance=±5% resistance=330 package=THT]
  R11 = Resistor [tolerance=±5% resistance=330 package=THT]
  R12 = Resistor [tolerance=±5% resistance=330 package=THT]
  R13 = Resistor [tolerance=±5% resistance=330 package=THT]
  R14 = Resistor [tolerance=±5% resistance=330 package=THT]
  R15 = Resistor [tolerance=±5% resistance=330 package=THT]
  R16 = Resistor [tolerance=±5% resistance=330 package=THT]
  U3 = 74HC595 [package="DIP16 [THT]"]
  R17 = Resistor [tolerance=±5% resistance=330 package=THT]
  R18 = Resistor [tolerance=±5% resistance=330 package=THT]
  R19 = Resistor [tolerance=±5% resistance=330 package=THT]
  R20 = Resistor [tolerance=±5% resistance=330 package=THT]
  R21 = Resistor [tolerance=±5% resistance=330 package=THT]
  R22 = Resistor [tolerance=±5% resistance=330 package=THT]
  R23 = Resistor [tolerance=±5% resistance=330 package=THT]
  R24 = Resistor [tolerance=±5% resistance=330 package=THT]
  U4 = 74HC595 [package="DIP16 [THT]"]
  R25 = Resistor [tolerance=±5% resistance=330 package=THT]
  R26 = Resistor [tolerance=±5% resistance=330 package=THT]
  R27 = Resistor [tolerance=±5% resistance=330 package=THT]
  R28 = Resistor [tolerance=±5% resistance=330 package=THT]
  R29 = Resistor [tolerance=±5% resistance=330 package=THT]
  R30 = Resistor [tolerance=±5% resistance=330 package=THT]
  R31 = Resistor [tolerance=±5% resistance=330 package=THT]
  R32 = Resistor [tolerance=±5% resistance=330 package=THT]
  U5 = 74HC595 [package="DIP16 [THT]"]
  U8 = 74HC595 [package="DIP16 [THT]"]
  U7 = 74HC595 [package="DIP16 [THT]"]
  U6 = 74HC595 [package="DIP16 [THT]"]
  R33 = Resistor [tolerance=±5% resistance=330 package=THT]
  R34 = Resistor [tolerance=±5% resistance=330 package=THT]
  R35 = Resistor [tolerance=±5% resistance=330 package=THT]
  R36 = Resistor [tolerance=±5% resistance=330 package=THT]
  R37 = Resistor [tolerance=±5% resistance=330 package=THT]
  R38 = Resistor [tolerance=±5% resistance=330 package=THT]
  R39 = Resistor [tolerance=±5% resistance=330 package=THT]
  R40 = Resistor [tolerance=±5% resistance=330 package=THT]
  R41 = Resistor [tolerance=±5% resistance=330 package=THT]
  R42 = Resistor [tolerance=±5% resistance=330 package=THT]
  R43 = Resistor [tolerance=±5% resistance=330 package=THT]
  R44 = Resistor [tolerance=±5% resistance=330 package=THT]
  R45 = Resistor [tolerance=±5% resistance=330 package=THT]
  R46 = Resistor [tolerance=±5% resistance=1k package=THT]
  R47 = Resistor [tolerance=±5% resistance=330 package=THT]
  R48 = Resistor [tolerance=±5% resistance=1k package=THT]
  R49 = Resistor [tolerance=±5% resistance=330 package=THT]
  R50 = Resistor [tolerance=±5% resistance=330 package=THT]
  R51 = Resistor [tolerance=±5% resistance=330 package=THT]
  R52 = Resistor [tolerance=±5% resistance=330 package=THT]
  R53 = Resistor [tolerance=±5% resistance=330 package=THT]
  R54 = Resistor [tolerance=±5% resistance=330 package=THT]
  R55 = Resistor [tolerance=±5% resistance=330 package=THT]
  R56 = Resistor [tolerance=±5% resistance=330 package=THT]
  R57 = Resistor [tolerance=±5% resistance=330 package=THT]
  R58 = Resistor [tolerance=±5% resistance=330 package=THT]
  R59 = Resistor [tolerance=±5% resistance=330 package=THT]
  R60 = Resistor [tolerance=±5% resistance=330 package=THT]
  R61 = Resistor [tolerance=±5% resistance=330 package=THT]
  R62 = Resistor [tolerance=±5% resistance=330 package=THT]
  R63 = Resistor [tolerance=±5% resistance=330 package=THT]
  R64 = Resistor [tolerance=±5% resistance=1k package=THT]
  R65 = Resistor [tolerance=±5% resistance=10k package=THT]
  LED1 = LEDs [package=led10mm]
  LED2 = LEDs [package=led10mm]
  LED3 = LEDs [package=led10mm]
  LED4 = LEDs [package=led10mm]
  LED5 = LEDs [package=led10mm]
  LED6 = LEDs [package=led10mm]
  LED7 = LEDs [package=led10mm]
  LED8 = LEDs [package=led10mm]
  LED9 = LEDs [package=led10mm]
  LED10 = LEDs [package=led10mm]
  LED11 = LEDs [package=led10mm]
  LED12 = LEDs [package=led10mm]
  LED13 = LEDs [package=led10mm]
  LED14 = LEDs [package=led10mm]
  LED15 = LEDs [package=led10mm]
  LED16 = LEDs [package=led10mm]
  LED17 = LEDs [package=led10mm]
  LED18 = LEDs [package=led10mm]
  LED19 = LEDs [package=led10mm]
  LED20 = LEDs [package=led10mm]
  LED21 = LEDs [package=led10mm]
  LED22 = LEDs [package=led10mm]
  LED23 = LEDs [package=led10mm]
  LED24 = LEDs [package=led10mm]
  LED25 = LEDs [package=led10mm]
  LED26 = LEDs [package=led10mm]
  LED27 = LEDs [package=led10mm]
  LED28 = LEDs [package=led10mm]
  LED29 = LEDs [package=led10mm]
  LED30 = LEDs [package=led10mm]
  LED31 = LEDs [package=led10mm]
  LED32 = LEDs [package=led10mm]
  LED33 = LEDs [package=led10mm]
  LED34 = LEDs [package=led10mm]
  LED35 = LEDs [package=led10mm]
  LED36 = LEDs [package=led10mm]
  LED37 = LEDs [package=led10mm]
  LED38 = LEDs [package=led10mm]
  LED39 = LEDs [package=led10mm]
  LED40 = LEDs [package=led10mm]
  LED41 = LEDs [package=led10mm]
  LED42 = LEDs [package=led10mm]
  LED43 = LEDs [package=led10mm]
  LED44 = LEDs [package=led10mm]
  LED45 = LEDs [package=led10mm]
  LED46 = LEDs [package=led10mm]
  LED47 = LEDs [package=led10mm]
  LED48 = LEDs [package=led10mm]
  LED49 = LEDs [package=led10mm]
  LED50 = LEDs [package=led10mm]
  LED51 = LEDs [package=led10mm]
  LED52 = LEDs [package=led10mm]
  LED54 = LEDs [package=led10mm]
  LED56 = LEDs [package=led10mm]
  LED57 = LEDs [package=led10mm]
  LED58 = LEDs [package=led10mm]
  LED59 = LEDs [package=led10mm]
  LED61 = LEDs [package=led10mm]
  LED63 = LEDs [package=led10mm]
  LED64 = LEDs [package=led10mm]
  Q1 = NPN-Transistor [package="TO92 [THT]"]
  7_Segment1 = 7 Segment Display
  7_Segment2 = 7 Segment Display
  7_Segment3 = 7 Segment Display
  7_Segment4 = 7 Segment Display
  Q2 = NPN-Transistor [package="TO92 [THT]"]
  Q3 = NPN-Transistor [package="TO92 [THT]"]
  Q4 = NPN-Transistor [package="TO92 [THT]"]
  U9 = HEF4543 [package=dil16]
  R66 = Resistor [tolerance=±5% resistance=330 package=THT]
  R67 = Resistor [tolerance=±5% resistance=330 package=THT]
  LED65 = LEDs [package=led10mm]
  LED67 = LEDs [package=led10mm]
  J1 = female pin header, 5 pins [form="♀ (female)"]
  S1 = Pushbutton [package="[THT]"]
  S2 = Pushbutton [package="[THT]"]
  S3 = Pushbutton [package="[THT]"]
  S4 = Pushbutton [package="[THT]"]
  Q5 = NPN-Transistor [package="TO92 [THT]"]
  R68 = Resistor [tolerance=±5% resistance=1k package=THT]

nets:
  GND: Componente1.GND, U1.GND, U1.OE, U2.GND, U2.OE, U3.GND, U3.OE, U4.GND, U4.OE, U5.GND, U5.OE, U8.GND, U8.OE, U7.GND, U7.OE, U6.GND, U6.OE, LED1.C, LED2.C, LED3.C, LED4.C, LED5.C, LED6.C, LED7.C, LED8.C, LED9.C, LED10.C, LED11.C, LED12.C, LED13.C, LED14.C, LED15.C, LED16.C, LED17.C, LED18.C, LED19.C, LED20.C, LED21.C, LED22.C, LED23.C, LED24.C, LED25.C, LED26.C, LED27.C, LED28.C, LED29.C, LED30.C, LED31.C, LED32.C, LED33.C, LED34.C, LED35.C, LED36.C, LED37.C, LED38.C, LED39.C, LED40.C, LED41.C, LED42.C, LED43.C, LED44.C, LED45.C, LED46.C, LED47.C, LED48.C, LED49.C, LED50.C, LED51.C, LED52.C, LED54.C, LED56.C, LED57.C, LED58.C, LED59.C, LED61.C, LED63.C, LED64.C, U9.PH, U9.BL, U9.GND, J1.pin5, S1.Pin_1, S1.Pin_2, S2.Pin_1, S2.Pin_2, S3.Pin_1, S3.Pin_2, S4.Pin_1, S4.Pin_2, Q5.E
  N1: Componente1.D2, R68.Pin_1
  N2: Componente1.D3, U9.D0
  N3: Componente1.D4, U9.D3
  N4: Componente1.D5, U9.D2
  N5: Componente1.D6, U9.D1
  N6: Componente1.D7, U1.SH_CP, U2.SH_CP, U3.SH_CP, U4.SH_CP, U5.SH_CP, U8.SH_CP, U7.SH_CP, U6.SH_CP, J1.pin2
  N7: Componente1.D8, J1.pin4
  N8: Componente1.D9, U1.DS, J1.pin3
  N9: Componente1.D10, S1.Pin_3, S1.Pin_4
  5V: Componente1.5V, R66.Pin_0, R67.Pin_0, J1.pin1
  N10: Componente1.D12/MISO, S3.Pin_4
  N11: Componente1.D13/SCK, S4.Pin_4
  N12: Componente1.D11/MOSI, S2.Pin_4
  N13: U1.Q1, R1.Pin_1
  N14: U1.Q2, R2.Pin_1
  N15: U1.Q3, R4.Pin_1
  N16: U1.Q4, R3.Pin_1
  N17: U1.Q5, R6.Pin_1
  N18: U1.Q6, R5.Pin_1
  N19: U1.Q7, R8.Pin_1
  N20: U1.Q7', U2.DS
  VCC: U1.MR, U1.VCC, U2.MR, U2.VCC, U3.MR, U3.VCC, U4.MR, U4.VCC, U5.MR, U5.VCC, U8.MR, U8.VCC, U7.MR, U7.VCC, U6.MR, U6.VCC, Q1.C, Q2.C, Q3.C, Q4.C, U9.LD, U9.VCC
  N21: U1.ST_CP, U2.ST_CP, U3.ST_CP, U4.ST_CP, U5.ST_CP, U8.ST_CP, U7.ST_CP, U6.ST_CP, R65.Pin_0
  N22: U1.Q0, R7.Pin_1
  N23: R1.Pin_0, LED2.A
  N24: R2.Pin_0, LED3.A
  N25: R3.Pin_0, LED5.A
  N26: R4.Pin_0, LED4.A
  N27: R5.Pin_0, LED6.A
  N28: R6.Pin_0, LED8.A
  N29: R7.Pin_0, LED1.A
  N30: R8.Pin_0, LED7.A
  N31: U2.Q1, R10.Pin_1
  N32: U2.Q2, R16.Pin_1
  N33: U2.Q3, R14.Pin_1
  N34: U2.Q4, R15.Pin_1
  N35: U2.Q5, R9.Pin_1
  N36: U2.Q6, R11.Pin_1
  N37: U2.Q7, R12.Pin_1
  N38: U2.Q7', U3.DS
  N39: U2.Q0, R13.Pin_1
  N40: R9.Pin_0, LED10.A
  N41: R10.Pin_0, LED14.A
  N42: R11.Pin_0, LED13.A
  N43: R12.Pin_0, LED15.A
  N44: R13.Pin_0, LED9.A
  N45: R14.Pin_0, LED16.A
  N46: R15.Pin_0, LED12.A
  N47: R16.Pin_0, LED11.A
  N48: U3.Q1, R18.Pin_1
  N49: U3.Q2, R24.Pin_1
  N50: U3.Q3, R22.Pin_1
  N51: U3.Q4, R23.Pin_1
  N52: U3.Q5, R17.Pin_1
  N53: U3.Q6, R19.Pin_1
  N54: U3.Q7, R20.Pin_1
  N55: U3.Q7', U4.DS
  N56: U3.Q0, R21.Pin_1
  N57: R17.Pin_0, LED21.A
  N58: R18.Pin_0, LED25.A
  N59: R19.Pin_0, LED31.A
  N60: R20.Pin_0, LED19.A
  N61: R21.Pin_0, LED17.A
  N62: R22.Pin_0, LED24.A
  N63: R23.Pin_0, LED32.A
  N64: R24.Pin_0, LED27.A
  N65: U4.Q1, R26.Pin_1
  N66: U4.Q2, R28.Pin_1
  N67: U4.Q3, R30.Pin_1
  N68: U4.Q4, R29.Pin_1
  N69: U4.Q5, R32.Pin_1
  N70: U4.Q6, R27.Pin_1
  N71: U4.Q7, R31.Pin_1
  N72: U4.Q7', U5.DS
  N73: U4.Q0, R25.Pin_1
  N74: R25.Pin_0, LED26.A
  N75: R26.Pin_0, LED30.A
  N76: R27.Pin_0, LED22.A
  N77: R28.Pin_0, LED18.A
  N78: R29.Pin_0, LED23.A
  N79: R30.Pin_0, LED20.A
  N80: R31.Pin_0, LED28.A
  N81: R32.Pin_0, LED29.A
  N82: U5.Q1, R36.Pin_1
  N83: U5.Q2, R47.Pin_1
  N84: U5.Q3, R38.Pin_1
  N85: U5.Q4, R49.Pin_1
  N86: U5.Q5, R62.Pin_1
  N87: U5.Q6, R61.Pin_1
  N88: U5.Q7, R43.Pin_1
  N89: U5.Q7', U6.DS
  N90: U5.Q0, R56.Pin_1
  N91: U8.Q1, R42.Pin_1
  N92: U8.Q2, R33.Pin_1
  N93: U8.Q3, R34.Pin_1
  N94: U8.Q4, R46.Pin_1
  N95: U8.Q5, R64.Pin_1
  N96: U8.Q6, R48.Pin_1
  N97: U8.Q7, R63.Pin_1
  N98: U8.DS, U7.Q7'
  N99: U8.Q0, R55.Pin_1
  N100: U7.Q1, R58.Pin_1
  N101: U7.Q2, R40.Pin_1
  N102: U7.Q3, R37.Pin_1
  N103: U7.Q4, R53.Pin_1
  N104: U7.Q5, R44.Pin_1
  N105: U7.Q6, R41.Pin_1
  N106: U7.Q7, R60.Pin_1
  N107: U7.DS, U6.Q7'
  N108: U7.Q0, R45.Pin_1
  N109: U6.Q1, R52.Pin_1
  N110: U6.Q2, R57.Pin_1
  N111: U6.Q3, R59.Pin_1
  N112: U6.Q4, R50.Pin_1
  N113: U6.Q5, R51.Pin_1
  N114: U6.Q6, R39.Pin_1
  N115: U6.Q7, R54.Pin_1
  N116: U6.Q0, R35.Pin_1
  N117: R33.Pin_0, LED51.A
  N118: R34.Pin_0, LED52.A
  N119: R35.Pin_0, LED45.A
  N120: R36.Pin_0, LED40.A
  N121: R37.Pin_0, LED50.A
  N122: R38.Pin_0, LED34.A
  N123: R39.Pin_0, LED44.A
  N124: R40.Pin_0, LED57.A
  N125: R41.Pin_0, LED58.A
  N126: R42.Pin_0, LED54.A
  N127: R43.Pin_0, LED33.A
  N128: R44.Pin_0, LED63.A
  N129: R45.Pin_0, LED64.A
  N130: R46.Pin_0, Q1.B
  N131: R47.Pin_0, LED41.A
  N132: R48.Pin_0, Q3.B
  N133: R49.Pin_0, LED43.A
  N134: R50.Pin_0, LED37.A
  N135: R51.Pin_0, LED39.A
  N136: R52.Pin_0, LED38.A
  N137: R53.Pin_0, LED59.A
  N138: R54.Pin_0, LED46.A
  N139: R55.Pin_0, LED61.A
  N140: R56.Pin_0, LED48.A
  N141: R57.Pin_0, LED35.A
  N142: R58.Pin_0, LED56.A
  N143: R59.Pin_0, LED36.A
  N144: R60.Pin_0, LED49.A
  N145: R61.Pin_0, LED42.A
  N146: R62.Pin_0, LED47.A
  N147: R63.Pin_0, Q4.B
  N148: R64.Pin_0, Q2.B
  N149: Q1.E, 7_Segment1.common_cathode
  N150: 7_Segment1.Segment_E, 7_Segment2.Segment_E, 7_Segment3.Segment_E, 7_Segment4.Segment_E, U9.C
  N151: 7_Segment1.Segment_D, 7_Segment2.Segment_D, 7_Segment3.Segment_D, 7_Segment4.Segment_D, U9.D
  N152: 7_Segment1.Segment_C, 7_Segment2.Segment_C, 7_Segment3.Segment_C, 7_Segment4.Segment_C, U9.E
  N153: 7_Segment1.Segment_B, 7_Segment2.Segment_B, 7_Segment3.Segment_B, 7_Segment4.Segment_B, U9.G
  N154: 7_Segment1.Segment_A, 7_Segment2.Segment_A, 7_Segment3.Segment_A, 7_Segment4.Segment_A, U9.F
  N155: 7_Segment1.Segment_F, 7_Segment2.Segment_F, 7_Segment3.Segment_F, 7_Segment4.Segment_F, U9.B
  N156: 7_Segment1.Segment_G, 7_Segment2.Segment_G, 7_Segment3.Segment_G, 7_Segment4.Segment_G, U9.A
  N157: 7_Segment2.common_cathode, Q2.E
  N158: 7_Segment3.common_cathode, Q3.E
  N159: 7_Segment4.common_cathode, Q4.E
  N160: R66.Pin_1, LED65.A
  N161: R67.Pin_1, LED67.A
  N162: LED65.C, LED67.C, Q5.C
  N163: Q5.B, R68.Pin_0
